# Fritzing sketch NMEA2000-Frequenz (saved by Fritzing 0.9.4)
breadboards: 2

parts:
  U1 = ESP32-38PinWide [part_number=ESP32-38PinWide]
  U2 = ESP32-38PinWide [part_number=ESP32-38PinWide]
  JP1 = Header 4 [package=molex-1x4_lock]
  JP2 = Header 4 [package=molex-1x4_lock]
  R1 = Rotary Potentiometer (Small) [maximum_resistance=100kΩ package=THT]

nets:
  N1: U1.3.3, JP1.1
  N2: U1.GND, JP1.2
  N3: U1.GPIO4, JP1.3
  N4: U1.GPIO5, JP1.4
  N5: U2.3.3, JP2.1, R1.leg2
  N6: U2.GPIO34, U2.GPIO35, R1.wiper
  N7: U2.GPIO26, U2.GPIO27
  N8: U2.GND, JP2.2, R1.leg1
  N9: U2.GPIO4, JP2.3
  N10: U2.GPIO5, JP2.4

custom parts:
  ESP32-38PinWide: Generic 38-Pin ESP32 with wide format (only access to one side of pins on a breadboard) based on Stephen Lilley's HiLetgo ESP-WROOM-32 ESP32 ESP-32S Development Board.
  Header 4: Header 4 Standard 4-pin 0.1 header. Use with straight break away headers (SKU : PRT-00116), right angle break away headers (PRT-00553), swiss pins (PRT-00743), machine pins (PRT-00117), and female headers (PRT-00115). Molex polarized connector foot print use with SKU : PRT-08231 with associated crimp pins and housings. 1MM SMD Version SKU: PRT-10208
